# Fritzing sketch Power-Supply-Adapter (saved by Fritzing 0.9.3b)
breadboards: 1

parts:
  J2 = Screw terminal - 2 pins [package=THT]
  D1 = Rectifier Diode [part_number=1N4001 package="300 mil [THT]"]
  J1 = Power Jack [package=power_jack_pth_lock]

nets:
  N1: J2.pin1, D1.cathode
  N2: J2.pin2, J1.GNDBREAK
  N3: D1.anode, J1.PWR

notes:
  4.5V output
  +
  -
  5.2V input
  +
  -
  0.7V diode drop
